# Fritzing sketch deployinator (saved by Fritzing 0.9.3b)
perfboards: 1

parts:
  WeMos_D1_Mini1 = WeMos D1 Mini
  R1 = Resistor [tolerance=±5% resistance=10k package=THT]
  R2 = Resistor [tolerance=±5% resistance=10k package=THT]
  R3 = Resistor [tolerance=±5% resistance=10k package=THT]
  Q1 = NPN-Transistor [package="TO92 [THT]"]
  HOLD_LED = LED - 5mm [color="Red (633nm)" package="5 mm [THT]"]
  R4 = Resistor [tolerance=±5% resistance=1k package=THT]
  R6 = Resistor [tolerance=±5% resistance=100 package=THT]
  Q2 = NPN-Transistor [package="TO92 [THT]"]
  DEPLOY_LED = LED - 5mm [color="Green (565nm)" package="5 mm [THT]"]
  R5 = Resistor [tolerance=±5% resistance=1k package=THT]
  R8 = Resistor [tolerance=±5% resistance=100 package=THT]
  R6_2 = Resistor [tolerance=±5% resistance=220 package=THT]
  R7 = Resistor [tolerance=±5% resistance=220 package=THT]
  DEPLOY = female pin header, 2 pins [form="♀ (female)"]
  J4 = female pin header, 2 pins [form="♀ (female)"]
  KEY = female pin header, 2 pins [form="♀ (female)"]
  HOLD = female pin header, 2 pins [form="♀ (female)"]
  OK_LED = LED - 5mm [color="Green (565nm)" package="5 mm [THT]"]
  PWR_LED = LED - 5mm [color="Orange (612nm)" package="5 mm [THT]"]

nets:
  3.3V: WeMos_D1_Mini1.3V3, DEPLOY.pin1, KEY.pin1, HOLD.pin1
  5V: WeMos_D1_Mini1.5V, R6.Pin_0, R8.Pin_0, J4.pin1
  N1: WeMos_D1_Mini1.D1, R4.Pin_0
  N2: WeMos_D1_Mini1.D2, R5.Pin_0
  N3: WeMos_D1_Mini1.D3, R6_2.Pin_0
  N4: WeMos_D1_Mini1.D4, R7.Pin_0
  N5: WeMos_D1_Mini1.D5, R1.Pin_1, KEY.pin2
  N6: WeMos_D1_Mini1.D6, R2.Pin_1, HOLD.pin2
  N7: WeMos_D1_Mini1.D7, R3.Pin_1, DEPLOY.pin2
  GND: WeMos_D1_Mini1.G, R1.Pin_0, R2.Pin_0, R3.Pin_0, Q1.E, Q2.E, J4.pin2, OK_LED.cathode, PWR_LED.cathode
  N8: Q1.B, R4.Pin_1
  N9: Q1.C, HOLD_LED.cathode
  N10: HOLD_LED.anode, R6.Pin_1
  N11: Q2.B, R5.Pin_1
  N12: Q2.C, DEPLOY_LED.cathode
  N13: DEPLOY_LED.anode, R8.Pin_1
  N14: R6_2.Pin_1, PWR_LED.anode
  N15: R7.Pin_1, OK_LED.anode

notes:
  LOL GLHF

custom parts:
  WeMos D1 Mini: The D1 mini is a mini wifi board based on ESP-8266EX.
